# Fritzing sketch scheme (saved by Fritzing 0.9.3b)

parts:
  S1 = H-Bridge with L298N
  Componente2 = Arduino Uno (Rev3) - ICSP
  M1 = DC Motor
  M2 = DC Motor
  BAT1 = BC9VPC [package=bc9vpc]

nets:
  N1: S1.12V, BAT1.V+
  GND: S1.GND, Componente2.GND, BAT1.V-
  5V: S1.5V, Componente2.5V
  N2: S1.ENA, Componente2.D5_PWM
  N3: S1.IN1, Componente2.D7
  N4: S1.IN2, Componente2.D6_PWM
  N5: S1.IN3, Componente2.D11_PWM/MOSI
  N6: S1.IN4, Componente2.ICSP_MISO, Componente2.D12/MISO
  N7: S1.ENB, Componente2.D10_PWM/SS
  N8: S1.M1-01, M1.pin_2
  N9: S1.M1-02, M1.pin_1
  N10: S1.M2-01, M2.pin_1
  N11: S1.M2-02, M2.pin_2

custom parts:
  H-Bridge with L298N: h-bridge
